# Fritzing sketch PUMP (saved by Fritzing 0.9.2b)

parts:
  WeMos_D1_Mini1 = WeMos D1 Mini
  KY-2 = Keyes Relay [package=THT]
  Capacitive_Soil_Moisture_Sensor2 = DFRobot Capacitive Soil Moisture Sensor V1.0 [part_number=SEN0193]
  Pump = mystery part, 2 pins [chip_label=?]

nets:
  5V: WeMos_D1_Mini1.5V, KY-2.signal, KY-2.C, Capacitive_Soil_Moisture_Sensor2.VCC
  N1: WeMos_D1_Mini1.A0, Capacitive_Soil_Moisture_Sensor2.A
  N2: WeMos_D1_Mini1.D4, KY-2.ground
  N3: WeMos_D1_Mini1.G, KY-2.power, Capacitive_Soil_Moisture_Sensor2.GND, Pump.pin1

notes:
  Pump

custom parts:
  WeMos D1 Mini: The D1 mini is a mini wifi board based on ESP-8266EX.
  Keyes Relay: The Keyes 5V relay module is suitable for SCM development, home appliance control. It uses a 5V~12V TIL control signal which can control DC / AC signal.
  DFRobot Capacitive Soil Moisture Sensor V1.0: DFRobot Capacitive Soil Moisture Sensor V1.0 This product measures soil moisture levels by capacitive sensing, rather than resistive sensing like other types of moisture sensor. It is made of a corrosion resistant material giving it a long service life. Insert it into soil and impress your friends with the real-time soil moisture data! The product includes an on-board voltage regulator which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
